// Logisim project control-logic.circ as structural Verilog: 1 circuit, main circuit control_logic
module control_logic (
  input  [31:0] Instruction,
  input  BrEq,
  input  BrLt,
  output PCSel,
  output RegWEn,
  output [2:0] ImmSel,
  output BrUn,
  output ASel,
  output BSel,
  output [3:0] ALUSel,
  output MemWEn,
  output [1:0] WBSel
);

  wire and_2_out, and_3_out, and_5_out, and_6_out, and_7_out, and_8_out, and_9_out, and_10_out, and_11_out,
       and_12_out, Btype, comparator_1_eq, comparator_2_eq, comparator_3_eq, comparator_4_eq,
       comparator_5_eq, comparator_6_eq, comparator_7_eq, comparator_8_eq, comparator_9_eq, comparator_10_eq,
       comparator_11_eq, comparator_12_eq, comparator_13_eq, comparator_14_eq, comparator_15_eq,
       comparator_16_eq, comparator_17_eq, compS, Itype, Jtype, not_2_out, not_3_out, not_4_out, op03, op6f,
       op13, op17, op33, op37, op63, op67, or_3_out, or_6_out, or_9_out, Stype, Utype;
  wire [2:0] and_13_out, and_14_out, and_15_out, and_16_out, and_17_out, bit_extender_5_out,
       bit_extender_6_out, bit_extender_7_out, bit_extender_8_out, bit_extender_9_out;
  wire [3:0] bit_extender_1_out, bit_extender_2_out, bit_extender_3_out, bit_extender_4_out,
       multiplexer_1_out, multiplexer_2_out, or_1_out, xor_1_out;
  wire [3:3] and_1_out;
  wire [15:0] rom_1_data;

  and and_1 (and_1_out[3], Instruction[25], op33);
  ROM #(.addrWidth(6), .dataWidth(16)) rom_1 (.data(rom_1_data));  // open: addr
  assign bit_extender_1_out = {{3{op6f}}, op6f};  // Bit_Extender bit_extender_1
  Comparator #(.mode("unsigned"), .width(3)) comparator_1 (
    .a(Instruction[14:12]), .b(3'b101), .eq(comparator_1_eq));  // open: gt, lt
  Comparator #(.mode("unsigned"), .width(7)) comparator_2 (
    .a(Instruction[6:0]), .b(7'b0000011), .eq(comparator_2_eq));  // open: gt, lt
  buf buffer_1 (op03, comparator_2_eq);
  Comparator #(.mode("unsigned"), .width(7)) comparator_3 (
    .a(Instruction[6:0]), .b(7'b0100011), .eq(comparator_3_eq));  // open: gt, lt
  buf buffer_2 (MemWEn, comparator_3_eq);
  Comparator #(.mode("unsigned"), .width(7)) comparator_4 (
    .a(Instruction[6:0]), .b(7'b1101111), .eq(comparator_4_eq));  // open: gt, lt
  buf buffer_3 (op6f, comparator_4_eq);
  Comparator #(.mode("unsigned"), .width(7)) comparator_5 (
    .a(Instruction[6:0]), .b(7'b1100111), .eq(comparator_5_eq));  // open: gt, lt
  buf buffer_4 (op67, comparator_5_eq);
  Comparator #(.mode("unsigned"), .width(7)) comparator_6 (
    .a(Instruction[6:0]), .b(7'b0110111), .eq(comparator_6_eq));  // open: gt, lt
  buf buffer_5 (op37, comparator_6_eq);
  Comparator #(.mode("unsigned"), .width(7)) comparator_7 (
    .a(Instruction[6:0]), .b(7'b0010111), .eq(comparator_7_eq));  // open: gt, lt
  buf buffer_6 (op17, comparator_7_eq);
  assign bit_extender_2_out = {{3{op03}}, op03};  // Bit_Extender bit_extender_2
  assign bit_extender_3_out = {{3{MemWEn}}, MemWEn};  // Bit_Extender bit_extender_3
  assign bit_extender_4_out = {{3{Btype}}, Btype};  // Bit_Extender bit_extender_4
  Comparator #(.mode("unsigned"), .width(7)) comparator_8 (
    .a(Instruction[31:25]), .b(7'b0100000), .eq(comparator_8_eq));  // open: gt, lt
  Comparator #(.mode("unsigned"), .width(7)) comparator_9 (
    .a(Instruction[6:0]), .b(7'b0110011), .eq(comparator_9_eq));  // open: gt, lt
  buf buffer_7 (op13, comparator_10_eq);
  Comparator #(.mode("unsigned"), .width(7)) comparator_10 (
    .a(Instruction[6:0]), .b(7'b0010011), .eq(comparator_10_eq));  // open: gt, lt
  assign or_1_out = bit_extender_2_out | bit_extender_3_out | bit_extender_4_out | bit_extender_1_out;  // OR_Gate or_1, 4 bits wide
  Multiplexer #(.width(4)) multiplexer_1 (.in0(4'b1100), .in1(4'b1101), .out(multiplexer_1_out), .sel(and_2_out));
  and and_2 (and_2_out, comparator_8_eq, comparator_1_eq);
  not not_1 (BSel, comparator_9_eq);
  buf buffer_8 (op33, comparator_9_eq);
  or or_2 (WBSel[1], op6f, op37, op67);
  Comparator #(.mode("unsigned"), .width(7)) comparator_11 (
    .a(Instruction[6:0]), .b(7'b1100011), .eq(comparator_11_eq));  // open: gt, lt
  assign xor_1_out = or_1_out ^ 4'b1111;  // XOR_Gate xor_1, 4 bits wide
  Multiplexer #(.width(4)) multiplexer_2 (
    .in0({and_1_out[3], Instruction[14:12]}), .in1(multiplexer_1_out), .out(multiplexer_2_out), .sel(or_3_out));
  or or_3 (or_3_out, and_3_out, and_5_out);
  and and_3 (and_3_out, comparator_8_eq, op33);
  nor nor_1 (ASel, Btype, op6f, op17);
  buf buffer_9 (op63, comparator_11_eq);
  assign ALUSel = xor_1_out & multiplexer_2_out;  // AND_Gate and_4, 4 bits wide
  and and_5 (and_5_out, comparator_1_eq, comparator_8_eq, op13);
  and and_6 (and_6_out, compS, Btype);
  buf buffer_10 (RegWEn, MemWEn);
  or or_4 (PCSel, and_6_out, op6f, op67);
  or or_5 (WBSel[0], op03, op37);
  or or_6 (or_6_out, op17, op37);
  or or_7 (Itype, op13, op67, op03);
  buf buffer_11 (Stype, MemWEn);
  buf buffer_12 (Btype, op63);
  buf buffer_13 (RegWEn, Utype);
  buf buffer_14 (Utype, or_6_out);
  buf buffer_15 (Jtype, op6f);
  Comparator #(.mode("unsigned"), .width(3)) comparator_12 (
    .a(Instruction[14:12]), .b(3'b000), .eq(comparator_12_eq));  // open: gt, lt
  Comparator #(.mode("unsigned"), .width(3)) comparator_13 (
    .a(Instruction[14:12]), .b(3'b101), .eq(comparator_13_eq));  // open: gt, lt
  not not_2 (not_2_out, BrLt);
  Comparator #(.mode("unsigned"), .width(3)) comparator_14 (
    .a(Instruction[14:12]), .b(3'b001), .eq(comparator_14_eq));  // open: gt, lt
  not not_3 (not_3_out, BrEq);
  Comparator #(.mode("unsigned"), .width(3)) comparator_15 (
    .a(Instruction[14:12]), .b(3'b111), .eq(comparator_15_eq));  // open: gt, lt
  not not_4 (not_4_out, BrLt);
  Comparator #(.mode("unsigned"), .width(3)) comparator_16 (
    .a(Instruction[14:12]), .b(3'b110), .eq(comparator_16_eq));  // open: gt, lt
  Comparator #(.mode("unsigned"), .width(3)) comparator_17 (
    .a(Instruction[14:12]), .b(3'b100), .eq(comparator_17_eq));  // open: gt, lt
  or or_8 (RegWEn, op13, op33, op03, op6f, op67);
  and and_7 (and_7_out, comparator_12_eq, BrEq);
  and and_8 (and_8_out, comparator_13_eq, or_9_out);
  or or_9 (or_9_out, BrEq, not_2_out);
  and and_9 (and_9_out, comparator_14_eq, not_3_out);
  and and_10 (and_10_out, comparator_15_eq, not_4_out);
  and and_11 (and_11_out, comparator_16_eq, BrLt);
  and and_12 (and_12_out, comparator_17_eq, BrLt);
  or or_10 (BrUn, comparator_15_eq, comparator_16_eq);
  assign bit_extender_5_out = {{2{Itype}}, Itype};  // Bit_Extender bit_extender_5
  assign bit_extender_6_out = {{2{Stype}}, Stype};  // Bit_Extender bit_extender_6
  assign bit_extender_7_out = {{2{Btype}}, Btype};  // Bit_Extender bit_extender_7
  assign bit_extender_8_out = {{2{Utype}}, Utype};  // Bit_Extender bit_extender_8
  assign bit_extender_9_out = {{2{Jtype}}, Jtype};  // Bit_Extender bit_extender_9
  assign and_13_out = 3'b000 & bit_extender_5_out;  // AND_Gate and_13, 3 bits wide
  assign and_14_out = 3'b001 & bit_extender_6_out;  // AND_Gate and_14, 3 bits wide
  assign and_15_out = 3'b010 & bit_extender_7_out;  // AND_Gate and_15, 3 bits wide
  assign and_16_out = 3'b011 & bit_extender_8_out;  // AND_Gate and_16, 3 bits wide
  assign and_17_out = 3'b100 & bit_extender_9_out;  // AND_Gate and_17, 3 bits wide
  or or_11 (compS, and_7_out, and_8_out, and_9_out, and_10_out, and_11_out, and_12_out);
  assign ImmSel = and_13_out | and_14_out | and_15_out | and_16_out | and_17_out;  // OR_Gate or_12, 3 bits wide

  // Other names for the same wires on the sheet: func3[2:0] = Instruction[14:12]; op23 = MemWEn; WB1bit = WBSel[0];
  //   WB2bit = WBSel[1]; OpCode[6:0] = Instruction[6:0]; func7[6:0] = Instruction[31:25]

  // Notes on the sheet:
  //   INPUTS to your circuit
  //   Connect ROM Input here ->
  //   ROM FOR CONTROL LOGIC
  //   DON'T CHANGE THE LOCATIONS OF THE INPUTS AND OUTPUTS!
  //   This is only if you choose to do the ROM option
  //   CONNECT
  //   WIRE
  //   TO
  //   USE
  //   ROM
  //   OUTPUT from your circuit
  //   Reminder: If using ROM, use combinational logic for PCSel
endmodule
