// Logisim project cpu.circ as structural Verilog: 1 circuit, main circuit cpu
module cpu (
  input  clk,
  input  [31:0] Instruction,
  input  [31:0] MemReadData,
  output [31:0] MemAddress,
  output [31:0] ProgramCounter,
  output [31:0] ra,
  output [31:0] sp,
  output [31:0] t0,
  output [31:0] t1,
  output [31:0] t2,
  output [31:0] s0,
  output [31:0] s1,
  output [31:0] a0,
  output [3:0] MemWriteMask,
  output [31:0] MemWriteData
);

  wire ASel, BrEq, BrLt, BrUn, BSel, MemWEn, PCSel, RegWEn;
  wire [1:0] WBSel;
  wire [2:0] ImmSel;
  wire [3:0] ALUSel;
  wire [31:0] DataToReg, ImmOut, Instruction_t, multiplexer_1_out, multiplexer_2_out, multiplexer_4_out,
       multiplexer_5_out, multiplexer_6_out, multiplexer_7_out, PCa4, regfile_1_readdata1,
       regfile_1_readdata2, register_1_q, register_2_q, register_3_q, WBReg;

  Adder #(.width(32)) adder_1 (.a(ProgramCounter), .b(32'h4), .out(PCa4));  // open: cin, cout
  Multiplexer #(.width(32)) multiplexer_1 (.in0(PCa4), .in1(MemAddress), .out(multiplexer_1_out), .sel(PCSel));
  Register #(.width(32)) PC (.D(multiplexer_1_out), .clk(clk), .Q(ProgramCounter));  // open: en, clr
  Multiplexer #(.width(32)) multiplexer_2 (.in0(Instruction), .in1(32'h13), .out(multiplexer_2_out), .sel(PCSel));
  Register #(.width(32)) register_1 (.D(multiplexer_2_out), .clk(clk), .Q(register_1_q));  // open: en, clr
  Register #(.width(32)) register_2 (.D(ProgramCounter), .clk(clk), .Q(register_2_q));  // open: en, clr
  Multiplexer #(.width(32)) multiplexer_3 (.in0(Instruction), .in1(register_1_q), .out(Instruction_t), .sel(1'b1));
  Multiplexer #(.width(32)) multiplexer_4 (
    .in0(ProgramCounter), .in1(register_2_q), .out(multiplexer_4_out), .sel(1'b1));
  regfile regfile_1 (
    .ReadIndex1(Instruction_t[19:15]), .ReadIndex2(Instruction_t[24:20]), .WriteIndex(Instruction_t[11:7]),
    .WriteData(WBReg), .RegWEn(RegWEn), .clk(clk), .ra(ra), .sp(sp), .t0(t0), .t1(t1), .t2(t2), .s0(s0),
    .s1(s1), .a0(a0), .ReadData1(regfile_1_readdata1), .ReadData2(regfile_1_readdata2));
  imm_gen imm_gen_1 (.Instruction(Instruction_t), .ImmSel(ImmSel), .Immediate(ImmOut));
  control_logic control_logic_1 (
    .Instruction(Instruction_t), .BrEq(BrEq), .BrLt(BrLt), .PCSel(PCSel), .RegWEn(RegWEn), .ImmSel(ImmSel),
    .BrUn(BrUn), .ASel(ASel), .BSel(BSel), .ALUSel(ALUSel), .MemWEn(MemWEn), .WBSel(WBSel));
  Multiplexer #(.width(32)) multiplexer_5 (
    .in0(multiplexer_4_out), .in1(regfile_1_readdata1), .out(multiplexer_5_out), .sel(ASel));
  Multiplexer #(.width(32)) multiplexer_6 (
    .in0(regfile_1_readdata2), .in1(ImmOut), .out(multiplexer_6_out), .sel(BSel));
  alu alu_1 (.A(multiplexer_5_out), .B(multiplexer_6_out), .ALUSel(ALUSel), .ALUResult(MemAddress));
  branch_comp branch_comp_1 (
    .BrData1(regfile_1_readdata1), .BrData2(regfile_1_readdata2), .BrUn(BrUn), .BrEq(BrEq), .BrLt(BrLt));
  Register #(.width(32)) register_3 (.D(PCa4), .clk(clk), .Q(register_3_q));  // open: en, clr
  Multiplexer #(.width(32)) multiplexer_7 (.in0(PCa4), .in1(register_3_q), .out(multiplexer_7_out), .sel(1'b1));
  Multiplexer #(.select(2), .width(32)) multiplexer_8 (
    .in0(MemAddress), .in1(DataToReg), .in2(multiplexer_7_out), .in3(ImmOut), .out(WBReg), .sel(WBSel));
  partial_load partial_load_1 (
    .Instruction(Instruction_t), .MemAddress(MemAddress), .DataFromMem(MemReadData), .DataToReg(DataToReg));
  partial_store partial_store_1 (
    .Instruction(Instruction_t), .MemAddress(MemAddress), .DataFromReg(regfile_1_readdata2), .MemWEn(MemWEn),
    .MemWriteMask(MemWriteMask), .DataToMem(MemWriteData));

  // Other names for the same wires on the sheet: ALURes[31:0] = MemAddress; Instruction_o[31:0] = Instruction;
  //   rd[4:0] = Instruction_t[11:7]; rs1[4:0] = Instruction_t[19:15]; rs2[4:0] = Instruction_t[24:20]

  // Notes on the sheet:
  //   To IMEM
  //   IMEM (do **NOT** move this)
  //   From IMEM
  //   Inputs/Outputs for testing. Do **NOT** move these.
  //   To DMEM
  //   DMEM (do **NOT** move this)
  //   From DMEM
endmodule
