// Logisim project partial-load.circ as structural Verilog: 1 circuit, main circuit partial_load
module partial_load (
  input  [31:0] Instruction,
  input  [31:0] MemAddress,
  input  [31:0] DataFromMem,
  output [31:0] DataToReg
);

  wire comparator_1_eq;
  wire [14:0] multiplexer_1_out_2;
  wire [16:0] bit_extender_2_out;
  wire [24:0] bit_extender_1_out;
  wire [31:0] shifter_1_out, shifter_2_out, shifter_3_out;
  wire [31:15] multiplexer_1_out;

  Comparator #(.width(7)) comparator_1 (.a(Instruction[6:0]), .b(7'b0000011), .eq(comparator_1_eq));  // open: gt, lt
  // AND_Gate and_1 is placed but not wired
  Shifter #(.shift("lr"), .width(32)) shifter_1 (.in(DataFromMem), .\dist (5'b01000), .out(shifter_1_out));
  Shifter #(.shift("lr"), .width(32)) shifter_2 (.in(DataFromMem), .\dist (5'b10000), .out(shifter_2_out));
  Shifter #(.shift("lr"), .width(32)) shifter_3 (.in(DataFromMem), .\dist (5'b11000), .out(shifter_3_out));
  Multiplexer #(.select(2), .width(32)) multiplexer_1 (
    .in0(DataFromMem), .in1(shifter_1_out), .in2(shifter_2_out), .in3(shifter_3_out),
    .out({multiplexer_1_out, multiplexer_1_out_2}), .sel(MemAddress[1:0]));
  assign bit_extender_1_out = {{24{multiplexer_1_out_2[7]}}, multiplexer_1_out_2[7]};  // Bit_Extender bit_extender_1
  assign bit_extender_2_out = {{16{multiplexer_1_out[15]}}, multiplexer_1_out[15]};  // Bit_Extender bit_extender_2
  Multiplexer #(.select(2), .width(32)) multiplexer_2 (
    .in0({bit_extender_1_out, multiplexer_1_out_2[6:0]}), .in1({bit_extender_2_out, multiplexer_1_out_2}),
    .in2({multiplexer_1_out, multiplexer_1_out_2}), .out(DataToReg), .sel(Instruction[13:12]));  // open: in3

  // Other names for the same wires on the sheet: opcode[6:0] = Instruction[6:0]; func3[2:0] = Instruction[14:12]

  // Notes on the sheet:
  //   INPUTS to your circuit
  //   DON'T CHANGE THE LOCATIONS OF THE INPUTS AND OUTPUTS!
  //   OUTPUT from your circuit
endmodule
