// Logisim project partial-store.circ as structural Verilog: 1 circuit, main circuit partial_store
module partial_store (
  input  [31:0] Instruction,
  input  [31:0] MemAddress,
  input  [31:0] DataFromReg,
  input  MemWEn,
  output [3:0] MemWriteMask,
  output [31:0] DataToMem
);

  wire comparator_1_eq, comparator_2_eq, comparator_3_eq;
  wire [3:0] and_1_out, and_2_out, and_3_out, bit_extender_1_out, bit_extender_2_out, bit_extender_3_out,
       bit_extender_4_out, or_1_out, shifter_4_out;
  wire [31:0] shifter_1_out, shifter_2_out, shifter_3_out;

  Comparator #(.width(3)) comparator_1 (.a(Instruction[14:12]), .b(3'b000), .eq(comparator_1_eq));  // open: gt, lt
  Comparator #(.width(3)) comparator_2 (.a(Instruction[14:12]), .b(3'b001), .eq(comparator_2_eq));  // open: gt, lt
  Comparator #(.width(3)) comparator_3 (.a(Instruction[14:12]), .b(3'b010), .eq(comparator_3_eq));  // open: gt, lt
  assign bit_extender_1_out = {{3{comparator_1_eq}}, comparator_1_eq};  // Bit_Extender bit_extender_1
  assign bit_extender_2_out = {{3{comparator_2_eq}}, comparator_2_eq};  // Bit_Extender bit_extender_2
  assign bit_extender_3_out = {{3{comparator_3_eq}}, comparator_3_eq};  // Bit_Extender bit_extender_3
  assign and_1_out = bit_extender_1_out & 4'b0001;  // AND_Gate and_1, 4 bits wide
  assign and_2_out = bit_extender_2_out & 4'b0011;  // AND_Gate and_2, 4 bits wide
  assign and_3_out = bit_extender_3_out & 4'b1111;  // AND_Gate and_3, 4 bits wide
  Shifter #(.width(32)) shifter_1 (.in(DataFromReg), .\dist (5'b01000), .out(shifter_1_out));
  Shifter #(.width(32)) shifter_2 (.in(DataFromReg), .\dist (5'b10000), .out(shifter_2_out));
  Shifter #(.width(32)) shifter_3 (.in(DataFromReg), .\dist (5'b11000), .out(shifter_3_out));
  assign or_1_out = and_1_out | and_2_out | and_3_out;  // OR_Gate or_1, 4 bits wide
  Shifter #(.width(4)) shifter_4 (.in(or_1_out), .\dist (MemAddress[1:0]), .out(shifter_4_out));
  Multiplexer #(.select(2), .width(32)) multiplexer_1 (
    .in0(DataFromReg), .in1(shifter_1_out), .in2(shifter_2_out), .in3(shifter_3_out), .out(DataToMem),
    .sel(MemAddress[1:0]));
  assign bit_extender_4_out = {{3{MemWEn}}, MemWEn};  // Bit_Extender bit_extender_4
  assign MemWriteMask = shifter_4_out & bit_extender_4_out;  // AND_Gate and_4, 4 bits wide

  // Other names for the same wires on the sheet: opcode[6:0] = Instruction[6:0]; func3[2:0] = Instruction[14:12]

  // Notes on the sheet:
  //   INPUTS to your circuit
  //   DON'T CHANGE THE LOCATIONS OF THE INPUTS AND OUTPUTS!
  //   OUTPUT from your circuit
endmodule
