// Logisim project regfile.circ as structural Verilog: 1 circuit, main circuit regfile
module regfile (
  input  [4:0] ReadIndex1,
  input  [4:0] ReadIndex2,
  input  [4:0] WriteIndex,
  input  [31:0] WriteData,
  input  RegWEn,
  input  clk,
  output [31:0] ra,
  output [31:0] sp,
  output [31:0] t0,
  output [31:0] t1,
  output [31:0] t2,
  output [31:0] s0,
  output [31:0] s1,
  output [31:0] a0,
  output [31:0] ReadData1,
  output [31:0] ReadData2
);

  wire WE0, WE1, WE2, WE3, WE4, WE5, WE6, WE7, WE8, WE9, WE10, WE11, WE12, WE13, WE14, WE15, WE16, WE17,
       WE18, WE19, WE20, WE21, WE22, WE23, WE24, WE25, WE26, WE27, WE28, WE29, WE30, WE31;
  wire [31:0] ix0, ix1, ix2, ix3, ix4, ix5, ix6, ix7, ix8, ix9, ix10, ix11, ix12, ix13, ix14, ix15, ix16,
       ix17, ix18, ix19, ix20, ix21, ix22, ix23, ix24, ix25, ix26, ix27, ix28, ix29, ix30, ix31, ox3, ox4,
       ox11, ox12, ox13, ox14, ox15, ox16, ox17, ox18, ox19, ox20, ox21, ox22, ox23, ox24, ox25, ox26, ox27,
       ox28, ox29, ox30, ox31;

  Multiplexer #(.select(5), .width(32)) multiplexer_1 (
    .in0({32{1'b0}}), .in1(ra), .in2(sp), .in3(ox3), .in4(ox4), .in5(t0), .in6(t1), .in7(t2), .in8(s0),
    .in9(s1), .in10(a0), .in11(ox11), .in12(ox12), .in13(ox13), .in14(ox14), .in15(ox15), .in16(ox16),
    .in17(ox17), .in18(ox18), .in19(ox19), .in20(ox20), .in21(ox21), .in22(ox22), .in23(ox23), .in24(ox24),
    .in25(ox25), .in26(ox26), .in27(ox27), .in28(ox28), .in29(ox29), .in30(ox30), .in31(ox31),
    .out(ReadData1), .sel(ReadIndex1));
  Multiplexer #(.select(5), .width(32)) multiplexer_2 (
    .in0({32{1'b0}}), .in1(ra), .in2(sp), .in3(ox3), .in4(ox4), .in5(t0), .in6(t1), .in7(t2), .in8(s0),
    .in9(s1), .in10(a0), .in11(ox11), .in12(ox12), .in13(ox13), .in14(ox14), .in15(ox15), .in16(ox16),
    .in17(ox17), .in18(ox18), .in19(ox19), .in20(ox20), .in21(ox21), .in22(ox22), .in23(ox23), .in24(ox24),
    .in25(ox25), .in26(ox26), .in27(ox27), .in28(ox28), .in29(ox29), .in30(ox30), .in31(ox31),
    .out(ReadData2), .sel(ReadIndex2));
  Register #(.width(32)) register_1 (.D(ix4), .en(WE4), .clk(clk), .Q(ox4));  // open: clr
  Register #(.width(32)) register_2 (.D(ix8), .en(WE8), .clk(clk), .Q(s0));  // open: clr
  Register #(.width(32)) register_3 (.D(ix12), .en(WE12), .clk(clk), .Q(ox12));  // open: clr
  Register #(.width(32)) register_4 (.D(ix16), .en(WE16), .clk(clk), .Q(ox16));  // open: clr
  Register #(.width(32)) register_5 (.D(ix20), .en(WE20), .clk(clk), .Q(ox20));  // open: clr
  Register #(.width(32)) register_6 (.D(ix24), .en(WE24), .clk(clk), .Q(ox24));  // open: clr
  Register #(.width(32)) register_7 (.D(ix28), .en(WE28), .clk(clk), .Q(ox28));  // open: clr
  Demultiplexer #(.select(5), .width(32)) demultiplexer_1 (
    .out0(ix0), .out1(ix1), .out2(ix2), .out3(ix3), .out4(ix4), .out5(ix5), .out6(ix6), .out7(ix7),
    .out8(ix8), .out9(ix9), .out10(ix10), .out11(ix11), .out12(ix12), .out13(ix13), .out14(ix14),
    .out15(ix15), .out16(ix16), .out17(ix17), .out18(ix18), .out19(ix19), .out20(ix20), .out21(ix21),
    .out22(ix22), .out23(ix23), .out24(ix24), .out25(ix25), .out26(ix26), .out27(ix27), .out28(ix28),
    .out29(ix29), .out30(ix30), .out31(ix31), .in(WriteData), .sel(WriteIndex));
  Demultiplexer #(.select(5)) demultiplexer_2 (
    .out0(WE0), .out1(WE1), .out2(WE2), .out3(WE3), .out4(WE4), .out5(WE5), .out6(WE6), .out7(WE7),
    .out8(WE8), .out9(WE9), .out10(WE10), .out11(WE11), .out12(WE12), .out13(WE13), .out14(WE14),
    .out15(WE15), .out16(WE16), .out17(WE17), .out18(WE18), .out19(WE19), .out20(WE20), .out21(WE21),
    .out22(WE22), .out23(WE23), .out24(WE24), .out25(WE25), .out26(WE26), .out27(WE27), .out28(WE28),
    .out29(WE29), .out30(WE30), .out31(WE31), .in(RegWEn), .sel(WriteIndex));
  Register #(.width(32)) register_8 (.D(ix1), .en(WE1), .clk(clk), .Q(ra));  // open: clr
  Register #(.width(32)) register_9 (.D(ix5), .en(WE5), .clk(clk), .Q(t0));  // open: clr
  Register #(.width(32)) register_10 (.D(ix9), .en(WE9), .clk(clk), .Q(s1));  // open: clr
  Register #(.width(32)) register_11 (.D(ix13), .en(WE13), .clk(clk), .Q(ox13));  // open: clr
  Register #(.width(32)) register_12 (.D(ix17), .en(WE17), .clk(clk), .Q(ox17));  // open: clr
  Register #(.width(32)) register_13 (.D(ix21), .en(WE21), .clk(clk), .Q(ox21));  // open: clr
  Register #(.width(32)) register_14 (.D(ix25), .en(WE25), .clk(clk), .Q(ox25));  // open: clr
  Register #(.width(32)) register_15 (.D(ix29), .en(WE29), .clk(clk), .Q(ox29));  // open: clr
  Register #(.width(32)) register_16 (.D(ix2), .en(WE2), .clk(clk), .Q(sp));  // open: clr
  Register #(.width(32)) register_17 (.D(ix6), .en(WE6), .clk(clk), .Q(t1));  // open: clr
  Register #(.width(32)) register_18 (.D(ix10), .en(WE10), .clk(clk), .Q(a0));  // open: clr
  Register #(.width(32)) register_19 (.D(ix14), .en(WE14), .clk(clk), .Q(ox14));  // open: clr
  Register #(.width(32)) register_20 (.D(ix18), .en(WE18), .clk(clk), .Q(ox18));  // open: clr
  Register #(.width(32)) register_21 (.D(ix22), .en(WE22), .clk(clk), .Q(ox22));  // open: clr
  Register #(.width(32)) register_22 (.D(ix26), .en(WE26), .clk(clk), .Q(ox26));  // open: clr
  Register #(.width(32)) register_23 (.D(ix30), .en(WE30), .clk(clk), .Q(ox30));  // open: clr
  Register #(.width(32)) register_24 (.D(ix3), .en(WE3), .clk(clk), .Q(ox3));  // open: clr
  Register #(.width(32)) register_25 (.D(ix7), .en(WE7), .clk(clk), .Q(t2));  // open: clr
  Register #(.width(32)) register_26 (.D(ix11), .en(WE11), .clk(clk), .Q(ox11));  // open: clr
  Register #(.width(32)) register_27 (.D(ix15), .en(WE15), .clk(clk), .Q(ox15));  // open: clr
  Register #(.width(32)) register_28 (.D(ix19), .en(WE19), .clk(clk), .Q(ox19));  // open: clr
  Register #(.width(32)) register_29 (.D(ix23), .en(WE23), .clk(clk), .Q(ox23));  // open: clr
  Register #(.width(32)) register_30 (.D(ix27), .en(WE27), .clk(clk), .Q(ox27));  // open: clr
  Register #(.width(32)) register_31 (.D(ix31), .en(WE31), .clk(clk), .Q(ox31));  // open: clr

  // Other names for the same wires on the sheet: ox1[31:0] = ra; ox2[31:0] = sp; ox5[31:0] = t0; ox6[31:0] = t1;
  //   ox7[31:0] = t2; ox8[31:0] = s0; ox9[31:0] = s1; ox10[31:0] = a0

  // Notes on the sheet:
  //   INPUTS to your circuit
  //   DON'T CHANGE THE LOCATIONS OF THE INPUTS AND OUTPUTS!
  //   These are DEBUG/TEST outputs from your circuit.
  //   OUTPUTS from your circuit
endmodule
